// Logisim project subleq.circ as structural Verilog: 2 circuits, main circuit main
module main (
);

  wire and_1_out, CLK_out, comparator_1_eq, comparator_2_eq, comparator_2_lt, demultiplexer_1_out0,
       demultiplexer_1_out1, demultiplexer_1_out2, demultiplexer_1_out3, not_1_out, not_2_out, not_3_out,
       or_1_out, or_2_out, or_3_out, RST_out;
  wire [1:0] STEP_q;
  wire [7:0] adder_1_out, controlled_buffer_1_out, controlled_buffer_3_out, INS_q, INS_q_2, INS_q_3, PC_q;
  wire [23:0] A_q, B_q, controlled_buffer_7_out, controlled_buffer_8_out, controlled_buffer_9_out,
       ram_1_data, subtractor_1_out;

  Demultiplexer #(.select(2), .disabled(0), .enable("false")) demultiplexer_1 (
    .out0(demultiplexer_1_out0), .out1(demultiplexer_1_out1), .out2(demultiplexer_1_out2),
    .out3(demultiplexer_1_out3), .in(not_1_out), .sel(STEP_q));
  not not_1 (not_1_out, and_1_out);
  assign controlled_buffer_1_out = or_3_out ? INS_q : 8'bz;  // Controlled_Buffer controlled_buffer_1
  assign controlled_buffer_1_out = not_2_out ? 8'h1 : 8'bz;  // Controlled_Buffer controlled_buffer_2
  not not_2 (not_2_out, or_3_out);
  Counter #(.width(2), .max('h3), .trigger("falling")) STEP (
    .Q(STEP_q), .clk(and_1_out));  // open: load, D, count, carry, clr
  LED HALT (.in(comparator_1_eq));
  Button RST (.out(RST_out));
  not not_3 (not_3_out, comparator_1_eq);
  Comparator #(.mode("unsigned")) comparator_1 (.a({8{1'b1}}), .b(PC_q), .eq(comparator_1_eq));  // open: gt, lt
  Register PC (.D(adder_1_out), .en(demultiplexer_1_out3), .Q(PC_q), .clk(and_1_out), .clr(RST_out));
  Adder adder_1 (.a(PC_q), .b(controlled_buffer_1_out), .out(adder_1_out));  // open: cin, cout
  assign controlled_buffer_3_out = demultiplexer_1_out0 ? PC_q : 8'bz;  // Controlled_Buffer controlled_buffer_3
  assign controlled_buffer_3_out = demultiplexer_1_out1 ? INS_q_2 : 8'bz;  // Controlled_Buffer controlled_buffer_4
  assign controlled_buffer_3_out = demultiplexer_1_out2 ? INS_q_3 : 8'bz;  // Controlled_Buffer controlled_buffer_5
  assign controlled_buffer_3_out = demultiplexer_1_out3 ? INS_q_2 : 8'bz;  // Controlled_Buffer controlled_buffer_6
  RAM #(.dataWidth(24)) ram_1 (
    .addr(controlled_buffer_3_out), .data(ram_1_data), .clk(and_1_out), .ld(or_1_out));  // open: sel, clr
  or or_1 (or_1_out, demultiplexer_1_out0, or_2_out);
  or or_2 (or_2_out, demultiplexer_1_out1, demultiplexer_1_out2);
  assign controlled_buffer_7_out = demultiplexer_1_out0 ? ram_1_data : 24'bz;  // Controlled_Buffer controlled_buffer_7
  assign controlled_buffer_8_out = demultiplexer_1_out1 ? ram_1_data : 24'bz;  // Controlled_Buffer controlled_buffer_8
  assign controlled_buffer_9_out = demultiplexer_1_out2 ? ram_1_data : 24'bz;  // Controlled_Buffer controlled_buffer_9
  assign ram_1_data = demultiplexer_1_out3 ? subtractor_1_out : 24'bz;  // Controlled_Buffer controlled_buffer_10
  Register #(.width(24)) INS (
    .D(controlled_buffer_7_out), .en(demultiplexer_1_out0), .Q({INS_q_3, INS_q_2, INS_q}), .clk(and_1_out));  // open: clr
  Register #(.width(24)) B (
    .D(controlled_buffer_8_out), .en(demultiplexer_1_out1), .Q(B_q), .clk(and_1_out));  // open: clr
  Register #(.width(24)) A (
    .D(controlled_buffer_9_out), .en(demultiplexer_1_out2), .Q(A_q), .clk(and_1_out));  // open: clr
  Subtractor #(.width(24)) subtractor_1 (.a(B_q), .b(A_q), .out(subtractor_1_out));  // open: bin, bout
  Comparator #(.width(24)) comparator_2 (
    .a(subtractor_1_out), .b({24{1'b0}}), .eq(comparator_2_eq), .lt(comparator_2_lt));  // open: gt
  Clock CLK (.out(CLK_out));
  and and_1 (and_1_out, CLK_out, not_3_out);
  or or_3 (or_3_out, comparator_2_eq, comparator_2_lt);
endmodule

module fetch_mem (
  input  [23:0] MEMDATA,
  input  [7:0] Addr,
  input  Enable,
  input  CLK,
  input  CLR,
  output [7:0] MEMADDR,
  output MEMLOAD,
  output [23:0] Value
);

  assign MEMADDR = Enable ? Addr : 8'bz;  // Controlled_Buffer controlled_buffer_1
  and and_1 (MEMLOAD, Enable, CLK);
  Register #(.width(24)) PC (.D(MEMDATA), .en(Enable), .Q(Value), .clk(CLK), .clr(CLR));

  // Notes on the sheet:
  //   Enable: pull=down
  //   CLR: pull=down
  //   MEMLOAD: pull=down
  //   CLK: pull=down
endmodule
